# Fritzing sketch Beacon-soldering (saved by Fritzing 0.9.2b)

parts:
  Bean = LightBlue Bean

nets:
  N1: Bean.D1, Bean.1#101, Bean.1#104, Bean.1#107
  N2: Bean.1#80, Bean.1#81, Bean.1#86, Bean.1#87, Bean.GND
  N3: Bean.1#83, Bean.1#84
  N4: Bean.1#89, Bean.1#93, Bean.1#95
  N5: Bean.1#92, Bean.1#98, Bean.BAT
  N6: Bean.1#100, Bean.1#110
  N7: Bean.1#102, Bean.1#103, Bean.1#108

notes:
  In grey: solder bridges
