# Fritzing sketch Beacon-design (saved by Fritzing 0.9.2b)
circuit board: 8.46667cm x 5.64444cm
breadboards: 1

parts:
  Beacon = Vibration Motor- ROB-08449 [part_number=(motor+lamp) package=vibe-motor-10mm]
  S1 = SWITCH-MOMENTARY-2 [package=reed_switch_plastic]
  Q1_MOSFET = Basic FET N-Channel [part_number=FQP30N06L package="TO220 [THT]"]
  Bean = LightBlue Bean
  U1 = mystery part, 3 pins [chip_label="Voltage Regulator" part_number=LD1117V33]
  R1 = Resistor [tolerance=±5% resistance=100k package=THT]

nets:
  5V: Beacon.+, S1.1, S1.2, U1.pin3
  CMD: Beacon.-, Q1_MOSFET.drain
  N1: Q1_MOSFET.gate, Bean.D1, R1.Pin_1
  GND: Q1_MOSFET.source, Bean.GND, U1.pin1, R1.Pin_0
  N2: Bean.BAT, U1.pin2
